# Fritzing sketch lab3 (saved by Fritzing 0.9.1b)
breadboards: 1

parts:
  Part1 = Arduino Nano (Rev3.0)
  U1 = LCD-16X2 [package=lcd-16x2]
  Q1 = PNP-Transistor [package="TO92 [THT]"]
  R1 = Resistor [tolerance=±5% resistance=10 package=THT]
  R2 = Resistor [tolerance=±5% resistance=10 package=THT]
  R3 = Resistor [tolerance=±5% resistance=100 package=THT]
  R4 = Resistor [tolerance=±5% resistance=100 package=THT]
  R5 = Resistor [tolerance=±5% resistance=100 package=THT]
  U2 = mystery part, 3 pins [chip_label=?]

nets:
  GND: Part1.GND, U1.VSS, U1.R_W, U1.K, Q1.C, R3.Pin_0, R4.Pin_0, R5.Pin_0, U2.pin3
  N1: Part1.D2, U1.RS
  N2: Part1.D3, U1.E
  N3: Part1.D8, U1.DB4
  N4: Part1.D9, U1.DB5
  N5: Part1.D10, U1.DB6
  N6: Part1.D11/MOSI, U1.DB7
  5V: Part1.5V, U1.VDD, Q1.E, R1.Pin_0, U2.pin2
  N7: Part1.A0, U2.pin1
  N8: U1.VO, Q1.B
  N9: U1.A, R1.Pin_1, R2.Pin_1
  N10: R3.Pin_1, R4.Pin_1, R5.Pin_1

notes:
  Moisture sensor as generic part.
